# Fritzing sketch Virus (saved by Fritzing 0.9.2b)

parts:
  Componente1 = RFID-RC522-v2
  Componente2 = Arduino Uno (Rev3)
  LED1 = RGB LED (com. cathode, rgb) [package="5 mm [THT]"]
  R1 = Resistor [tolerance=±5% resistance=330 package=THT]

nets:
  N1: Componente1.SDA, Componente2.D10_PWM/SS
  N2: Componente1.SCK, Componente2.D13/SCK
  N3: Componente1.MOSI, Componente2.D11_PWM/MOSI
  N4: Componente1.MISO, Componente2.D12/MISO
  GND: Componente1.GND, Componente2.GND
  N5: Componente1.RST, Componente2.D9_PWM
  3.3V: Componente1.3.3V, Componente2.3V3
  N6: Componente2.D5_PWM, LED1.red_anode
  N7: Componente2.D6_PWM, LED1.green_anode
  N8: Componente2.D7, LED1.blue_anode
  N9: Componente2.5V, R1.Pin_1
  N10: LED1.common_cathode, R1.Pin_0

notes:
  3,3V
  5V
  13~9
  7~5

custom parts:
  RFID-RC522-v2: A simple China made RFID-RC522 Reader; do check the pin labels, as this is a MFRC522 based clone.
